# Fritzing sketch sketch (saved by Fritzing 1.0.5)

parts:
  U1 = LuaNode32 / ESP32 [part_number=ESP32S-PIN30]
  A1 = max485 HW-519 module
  JP1 = Header 4 [package=jst-4-pth]

nets:
  N1: U1.GND, A1.Pin_4, JP1.4
  N2: U1.Vin, JP1.1
  N3: U1.3V3, A1.Pin_1
  N4: U1.RX2, A1.Pin_3
  N5: U1.TX2, A1.Pin_2
  N6: A1.Pin_6, JP1.3
  N7: A1.Pin_7, JP1.2

notes:
  +5V
  A+
  B-
  GND

custom parts:
  LuaNode32 / ESP32: New Image for LuaNode32 DOIT ESP32 DEVKIT V1. Base parts from LuaNode32 / ESP32 ESP32 based LuaNode32 by G.Noorlander DOIT Esp32 DevKit v1 (30 pins long, 11 pins width) by Werner Rothschopf (modified by vanepp Dec 2018)
  max485 HW-519 module: Module,3.3V-5.5V 485 to Serial UART Level Mutual Conversion Hardware Automatic Flow Control Module.
